// Logisim project ALU Controler.circ as structural Verilog: 3 circuits, main circuit main
module main (
  input  ALUop,
  input  [5:0] OPcode,
  input  [5:0] FuncCode,
  output [3:0] out_4,
  output Write_HI_LO
);

  wire and_4_out;
  wire [1:0] nor_1_out;
  wire [2:2] or_1_out;
  wire [3:0] and_3_out, multiplexer_1_out, multiplexer_2_out;

  or or_1 (or_1_out[2], FuncCode[2], FuncCode[4]);
  and and_1 (and_3_out[3], OPcode[3], OPcode[1]);
  and and_2 (and_3_out[2], OPcode[2], ~OPcode[1]);  // AND_Gate
  and and_3 (and_3_out[0], OPcode[3], ~OPcode[2], OPcode[1]);  // AND_Gate
  Multiplexer #(.width(4), .enable("false")) multiplexer_1 (
    .in0(4'b1001), .in1({and_3_out[3:2], OPcode[0], and_3_out[0]}), .out(multiplexer_1_out), .sel(OPcode[3]));
  and and_4 (and_4_out, FuncCode[3], FuncCode[4], ~FuncCode[5]);  // AND_Gate
  Multiplexer #(.select(2), .width(4), .enable("false")) multiplexer_2 (
    .in0(multiplexer_1_out), .in1({FuncCode[3], or_1_out[2], FuncCode[0], FuncCode[1]}), .in2(FuncCode[3:0]),
    .in3(FuncCode[3:0]), .out(multiplexer_2_out), .sel(nor_1_out));
  and and_5 (nor_1_out[1], OPcode[5], OPcode[4], OPcode[3], OPcode[2], OPcode[1], OPcode[0]);
  nor nor_1 (nor_1_out[0], OPcode[5], OPcode[4], OPcode[3], OPcode[2], OPcode[1], OPcode[0]);
  Multiplexer #(.width(4), .enable("false")) multiplexer_3 (
    .in0(multiplexer_2_out), .in1(4'b0000), .out(out_4), .sel(ALUop));
  and and_6 (Write_HI_LO, nor_1_out[0], and_4_out);

  // Other names for the same wires on the sheet: Sum = ALUop
endmodule

module ALUOp (
  input  ALUOp1,
  input  ALUOp2,
  input  ALUOp3,
  output AC1,
  output AC2,
  output AC3,
  output AC4
);

  wire not_1_out;

  not not_1 (not_1_out, ALUOp1);
  and and_1 (AC4, not_1_out, ALUOp3);

  assign AC1 = 1'b0;
  assign AC2 = 1'b0;
  assign AC3 = 1'b0;
endmodule

module FuncDecoder (
  input  F1,
  input  F2,
  input  F3,
  input  F4,
  input  F5,
  input  F6,
  output AC1,
  output AC2,
  output AC3,
  output AC4
);

  wire and_1_out, not_1_out;

  or or_1 (AC2, F3, F2);
  or or_2 (AC3, F4, F2);
  not not_1 (not_1_out, F2);
  and and_1 (and_1_out, not_1_out, F5);
  or or_3 (AC4, F6, and_1_out);

  assign AC1 = 1'b0;
endmodule
