// Logisim project Control Unit.circ as structural Verilog: 1 circuit, main circuit main
module main (
  input  Clock,
  input  Immediate,
  input  Start,
  input  nLo_Hi,
  input  nPush_Pop,
  input  Reset,
  input  kbd_Available,
  input  [2:0] Operation,
  input  [5:0] Op_code,
  input  nR_W_Mem,
  input  [5:0] Func_code,
  input  [3:0] Read_Ram,
  input  [3:0] Write_Ram,
  output ALU_A_SELECTOR,
  output Access_SP,
  output [1:0] ALU_B_SELECTOR,
  output [1:0] Write_SP,
  output Save_ALU_Result,
  output Data_In_Selector,
  output Take_Direct_ALU_Op,
  output Write_RF,
  output Chip_Select,
  output Write_Instruction,
  output [1:0] RAM_Address_Selector,
  output Update_PC,
  output Write_RAM_2,
  output Try_jump
);

  wire [3:0] Mem_Time;

  Multiplexer #(.width(4), .enable("false")) multiplexer_1 (
    .in0(Read_Ram), .in1(Write_Ram), .out(Mem_Time), .sel(nR_W_Mem));

  // Other names for the same wires on the sheet: Clk = Clock; Hi = nLo_Hi; Imm = Immediate; IR_W_Mem = nR_W_Mem;
  //   kbdA = kbd_Available; Pop = nPush_Pop; Read_Time[3:0] = Read_Ram

  // Notes on the sheet:
  //   Inputs
  //   Control Signals
  //   ALU Signals
  //   RF Signals
  //   Output
  //   Memory Signals
  //   Misc Signals
endmodule
