// Logisim project ControlUnit.circ as structural Verilog: 1 circuit, main circuit main
module main (
);

  // Main_Control_Unit_main main_1: pin names not known
  // ALU_Controler_main main_2: pin names not known
endmodule
