// Logisim project Main Control Unit.circ as structural Verilog: 3 circuits, main circuit main
module main (
  input  Zero,
  input  Clock,
  input  SignLess,
  input  Reset,
  input  IsMult,
  input  [5:0] OpCode,
  input  MemReady,
  input  [5:0] FuncCode,
  output IorD,
  output ALU_Source_A,
  output MemRead,
  output MemWrite,
  output [1:0] ALU_Source_B,
  output IRWrite,
  output [2:0] ALUOp,
  output PCWrite,
  output Branch,
  output [1:0] RegDst,
  output [1:0] PCSource,
  output halt,
  output TTYWrite,
  output [1:0] MemToReg,
  output KbdRead,
  output RegWrite,
  output HiLoSelector,
  output HiLoWrite,
  output ReadSp,
  output ReadRsAsB,
  output ZeroEx
);

  wire ALUOp101, ALUOp_011, ALUOp_100, ALUOp_110, ALUOp_111, ALUOp_Diff_b, ALUOp_R, ALUOp_Sum_a, ALUOp_Sum_b,
       ALUOp_Sum_c, ALUOp_Sum_d, ALUOp_Sum_e, ALUOp_Sum_f, ALUOp_Sum_g, AluSrcB_0_b, and_1_out, IorD_b,
       IorD_c, IorD_d, IorD_e, MemToReg_11_b, MemToReg_a, MemToReg_c, MemWrite_a, MovHiLo, MovHL, or_1_out,
       or_2_out, or_5_out, or_6_out, or_14_out, or_15_out, ReadSP_a, ReadSP_b, ReadSP_c, RegDst_01_c,
       RegWrite_a;
  wire [3:0] Op_Dec, opdec_1_out_2;
  wire [4:0] multiplexer_1_out, multiplexer_9_out, Next_S0, Next_S1, Next_S2, Next_S3, Next_S5, Next_S6,
       Next_S16, Next_S18, StateReg_q;

  or or_1 (or_1_out, ALUOp_Sum_a, ALUOp_Diff_b, ALUOp_Sum_f);
  or or_2 (or_2_out, ALUOp_Sum_c, ALUOp_Sum_d, ALUOp_011, ALUOp_100, ALUOp101, ALUOp_110);
  or or_3 (PCWrite, IRWrite, ALUOp_Sum_g, PCSource[1]);
  or or_4 (ALU_Source_A, ALUOp_Sum_c, ALUOp_R, Branch, ALUOp_Sum_d, ALUOp_011, ALUOp_100, ALUOp101, ALUOp_Diff_b, ALUOp_Sum_e, ALUOp_Sum_f, ALUOp_110, ALUOp_Sum_g);
  or or_5 (or_5_out, ALUOp_Sum_a, ALUOp_Sum_b, ALUOp_Sum_c, ALUOp_Sum_d, ALUOp_Sum_e, ALUOp_Sum_f, ALUOp_Sum_g);
  or or_6 (or_6_out, Branch, ALUOp_Diff_b);
  or or_7 (ALU_Source_B[0], or_1_out, ALUOp_Sum_b);
  or or_8 (ALU_Source_B[1], ALUOp_Sum_b, or_2_out);
  Priority_Encoder priority_encoder_1 (
    .in0(or_5_out), .in1(ALUOp_R), .in2(or_6_out), .in3(ALUOp_011), .in4(ALUOp_100), .in5(ALUOp101),
    .in6(ALUOp_110), .in7(ALUOp_111), .out(ALUOp));  // open: en_in, gs, en_out
  or or_9 (IorD, IorD_e, IorD_b, IorD_c, IorD_d);
  and and_1 (and_1_out, Branch, MovHiLo);
  or or_10 (MemRead, ALUOp_Sum_a, IorD_b, IorD_e);
  or or_11 (MemWrite, MemWrite_a, IorD_d);
  or or_12 (RegDst[0], AluSrcB_0_b, Branch, MemToReg_11_b, RegDst_01_c, KbdRead);
  or or_13 (RegDst[1], IorD_d, MemToReg_a);
  or or_14 (or_14_out, IorD_d, MemToReg_c, MemToReg_a, AluSrcB_0_b);
  or or_15 (or_15_out, and_1_out, MemToReg_11_b);
  or or_16 (RegWrite, RegWrite_a, AluSrcB_0_b, Branch, MemToReg_c, MemToReg_11_b, IorD_d, RegDst_01_c, MemToReg_a, KbdRead);
  or or_17 (ReadSp, ReadSP_a, ReadSP_b, ReadSP_c);
  or or_18 (ReadRsAsB, ALUOp_Diff_b, IorD_d);
  or or_19 (ZeroEx, ALUOp_011, ALUOp_100, ALUOp101);
  OpDec opdec_1 (.in_1(OpCode), .out_2(opdec_1_out_2));
  and and_2 (MovHiLo, ~FuncCode[0], FuncCode[2], ~FuncCode[3], FuncCode[4], ~FuncCode[5]);  // AND_Gate
  or or_20 (MemToReg[0], or_14_out, or_15_out);
  or or_21 (MemToReg[1], or_15_out, KbdRead);
  OpFuncDec opfuncdec_1 (.OpCode(opdec_1_out_2), .FunCode(FuncCode), .out_3(Op_Dec), .out_4(MovHL));
  // Probe on Op_Dec
  Register #(.width(5)) StateReg (.D(multiplexer_1_out), .Q(StateReg_q), .clk(Clock), .clr(Reset));  // open: en
  Decoder #(.select(5), .enable("false")) decoder_1 (
    .out0(ALUOp_Sum_a), .out1(ALUOp_Sum_b), .out2(ALUOp_Sum_c), .out3(IorD_b), .out4(RegWrite_a),
    .out5(IorD_c), .out6(ALUOp_R), .out7(AluSrcB_0_b), .out8(Branch), .out9(ALUOp_Sum_d), .out10(MemToReg_c),
    .out11(PCSource[1]), .out12(ALUOp_011), .out13(ALUOp_100), .out14(ALUOp101), .out15(ReadSP_a),
    .out16(IorD_d), .out17(ReadSP_b), .out18(IorD_e), .out19(RegDst_01_c), .out20(ReadSP_c),
    .out21(ALUOp_110), .out22(ALUOp_Sum_g), .out23(halt), .out24(TTYWrite), .out25(ALUOp_111),
    .out26(KbdRead), .out27(MemToReg_11_b), .out28(ALUOp_Diff_b), .out29(ALUOp_Sum_e), .out30(ALUOp_Sum_f),
    .out31(MemToReg_a), .sel(StateReg_q));
  Multiplexer #(.select(5), .width(5)) multiplexer_1 (
    .in0(Next_S0), .in1(Next_S1), .in2(Next_S2), .in3(Next_S3), .in4({5{1'b0}}), .in5(Next_S5),
    .in6(Next_S6), .in7({5{1'b0}}), .in8({5{1'b0}}), .in9(5'b01010), .in10({5{1'b0}}), .in11({5{1'b0}}),
    .in12(5'b01010), .in13(5'b01010), .in14(5'b01010), .in15(5'b11100), .in16(Next_S16), .in17(5'b11101),
    .in18(Next_S18), .in19(5'b10100), .in20(5'b11110), .in21(5'b01010), .in22({5{1'b0}}), .in23(5'b10111),
    .in24({5{1'b0}}), .in25(5'b00111), .in26({5{1'b0}}), .in27({5{1'b0}}), .in28(5'b10000), .in29(5'b10010),
    .in30({5{1'b1}}), .in31({5{1'b0}}), .out(multiplexer_1_out), .sel(StateReg_q));  // open: en
  Multiplexer #(.width(5), .enable("false")) multiplexer_2 (
    .in0({5{1'b0}}), .in1(5'b00001), .out(Next_S0), .sel(MemReady));
  Multiplexer #(.width(5), .enable("false")) multiplexer_3 (
    .in0(5'b00011), .in1(5'b00101), .out(Next_S2), .sel(OpCode[3]));
  Multiplexer #(.width(5), .enable("false")) multiplexer_4 (
    .in0(5'b00011), .in1(5'b00100), .out(Next_S3), .sel(MemReady));
  Multiplexer #(.width(5), .enable("false")) multiplexer_5 (
    .in0(5'b00101), .in1({5{1'b0}}), .out(Next_S5), .sel(MemReady));
  Multiplexer #(.width(5), .enable("false")) multiplexer_6 (
    .in0(5'b00111), .in1({5{1'b0}}), .out(Next_S6), .sel(IsMult));
  Multiplexer #(.width(5), .enable("false")) multiplexer_7 (
    .in0(5'b10000), .in1({5{1'b0}}), .out(Next_S16), .sel(MemReady));
  Multiplexer #(.width(5), .enable("false")) multiplexer_8 (
    .in0(5'b10010), .in1(5'b10011), .out(Next_S18), .sel(MemReady));
  Multiplexer #(.select(4), .width(5), .enable("false")) multiplexer_9 (
    .in0(5'b00010), .in1(5'b00110), .in2(5'b01000), .in3(5'b01001), .in4(5'b10101), .in5(5'b01100),
    .in6(5'b01101), .in7(5'b01110), .in8(5'b01111), .in9(5'b10001), .in10(5'b01011), .in11(5'b10110),
    .in12(5'b11000), .in13(5'b11001), .in14(5'b11010), .in15(5'b10111), .out(multiplexer_9_out), .sel(Op_Dec));
  Multiplexer #(.width(5), .enable("false")) multiplexer_10 (
    .in0(multiplexer_9_out), .in1(5'b11011), .out(Next_S1), .sel(MovHL));
  and and_3 (IRWrite, MemReady, ALUOp_Sum_a);
  and and_4 (HiLoWrite, IsMult, ALUOp_R);

  assign HiLoSelector = FuncCode[1];
  assign PCSource[0] = Branch;

  // Other names for the same wires on the sheet: Clk = Clock; Func_Code[5:0] = FuncCode; HILO_WR = HiLoWrite;
  //   Op_Code[5:0] = OpCode; sltiSign = OpCode[0]; lw_sw = OpCode[3]; ALUOp_Diff_a = Branch; AluSrcA_c = Branch;
  //   AluSrcB_0_c = Branch; MemToReg_11 = Branch; PCSource_01 = Branch; RegDst_01_b = Branch; RegWrite_c = Branch;
  //   S8_BranchComp = Branch; PCSource_10 = PCSource[1]; PCWrite_b = PCSource[1]; S11_Jump = PCSource[1];
  //   PCWrite_a = IRWrite; AluSrcB_01_a = ALUOp_Sum_a; MemRead_a = ALUOp_Sum_a; S0_Fetch = ALUOp_Sum_a;
  //   AluSrcB_11 = ALUOp_Sum_b; S1_Decode = ALUOp_Sum_b; AluSrcA_a = ALUOp_Sum_c; AluSrcB_10_a = ALUOp_Sum_c;
  //   S2_MemAdr = ALUOp_Sum_c; MemRead_b = IorD_b; S3_MemRead = IorD_b; S4_MemWB = RegWrite_a; MemWrite_a_t = IorD_c;
  //   S5_MemWrite = IorD_c; AluSrcA_b = ALUOp_R; AluSrcB_0_a = ALUOp_R; S6_Execution = ALUOp_R;
  //   MemToReg_d = AluSrcB_0_b; RegDst_01_a = AluSrcB_0_b; RegWrite_b = AluSrcB_0_b; S7_AluWB = AluSrcB_0_b;
  //   AluSrcA_d = ALUOp_Sum_d; AluSrcB_10_b = ALUOp_Sum_d; S9_AddiEx = ALUOp_Sum_d; RegWrite_d = MemToReg_c;
  //   S10_ImmWB = MemToReg_c; S15_PushEx = ReadSP_a; MemToReg_e = IorD_d; MemWrite_b = IorD_d; ReadRsAsB_b = IorD_d;
  //   RegDst_10_a = IorD_d; RegWrite_e = IorD_d; S16_PushWrite = IorD_d; S17_PopAddr = ReadSP_b; MemRead_c = IorD_e;
  //   S18_PopRead = IorD_e; RegWrite_f = RegDst_01_c; S19_PopWB = RegDst_01_c; S20_PopUpdateSP = ReadSP_c;
  //   AluSrcA_k = ALUOp_110; AluSrcB_10_g = ALUOp_110; S21_SltiEx = ALUOp_110; AluSrcA_l = ALUOp_Sum_g;
  //   AluSrcB_0_d = ALUOp_Sum_g; PCWrite_c = ALUOp_Sum_g; S22_JumpReg = ALUOp_Sum_g; S23_Halt = halt;
  //   S24_Tty = TTYWrite; S25_Rnd = ALUOp_111; MemToReg_10 = KbdRead; RegDst_01_d = KbdRead; RegWrite_h = KbdRead;
  //   S26_Kbd = KbdRead; RegDst_01_e = MemToReg_11_b; RegWrite_i = MemToReg_11_b; S27_MovHL = MemToReg_11_b;
  //   AluSrcA_h = ALUOp_Diff_b; AluSrcB_01_b = ALUOp_Diff_b; ReadRsAsB_t = ALUOp_Diff_b; S28 = ALUOp_Diff_b;
  //   AluSrcA_i = ALUOp_Sum_e; S29 = ALUOp_Sum_e; AluSrcA_j = ALUOp_Sum_f; AluSrcB_01_c = ALUOp_Sum_f;
  //   S30 = ALUOp_Sum_f; RegDst_10_b = MemToReg_a; RegWrite_g = MemToReg_a; S31 = MemToReg_a; AluSrcA_e = ALUOp_011;
  //   AluSrcB_10_c = ALUOp_011; S12_AndiEx = ALUOp_011; ZeroEx_a = ALUOp_011; AluSrcA_f = ALUOp_100;
  //   AluSrcB_10_d = ALUOp_100; S13_OriEx = ALUOp_100; ZeroEx_b = ALUOp_100; AluSrcA_g = ALUOp101;
  //   AluSrcB_10_e = ALUOp101; S14_XoriEx = ALUOp101; ZeroEx_c = ALUOp101

  // Notes on the sheet:
  //   Inputs
  //   ALU Signals
  //   Control Signals
  //   3Er bit de ALUOp
  //   Misc Signals
  //   Output
  //   MIAS
  //   Memory Signals
  //   RF Signals
  //   Operation Decoder
  //   Cambiar de Fetch a Decode
  //   Proximo Estado
  //   Señales de estado
endmodule

module OpDec (
  input  [5:0] in_1,
  output [3:0] out_2
);

  wire and_1_out, and_2_out, and_3_out, and_4_out, and_5_out, and_6_out, and_7_out, and_8_out, and_9_out,
       and_10_out, and_11_out, and_12_out, and_13_out, not_1_out, not_2_out, not_3_out, not_4_out, not_5_out,
       not_6_out, not_7_out, not_8_out, not_9_out, not_10_out, not_11_out, not_12_out, not_13_out,
       not_14_out, not_15_out, not_16_out, not_17_out, not_18_out, not_19_out, not_20_out, not_21_out;

  not not_1 (not_1_out, in_1[5]);
  not not_2 (not_2_out, in_1[3]);
  not not_3 (not_3_out, in_1[2]);
  not not_4 (not_4_out, in_1[2]);
  not not_5 (not_5_out, in_1[1]);
  not not_6 (not_6_out, in_1[0]);
  not not_7 (not_7_out, in_1[5]);
  not not_8 (not_8_out, in_1[5]);
  not not_9 (not_9_out, in_1[1]);
  not not_10 (not_10_out, in_1[3]);
  not not_11 (not_11_out, in_1[0]);
  not not_12 (not_12_out, in_1[3]);
  not not_13 (not_13_out, in_1[0]);
  not not_14 (not_14_out, in_1[5]);
  not not_15 (not_15_out, in_1[2]);
  not not_16 (not_16_out, in_1[1]);
  not not_17 (not_17_out, in_1[4]);
  not not_18 (not_18_out, in_1[2]);
  not not_19 (not_19_out, in_1[1]);
  not not_20 (not_20_out, in_1[0]);
  not not_21 (not_21_out, in_1[0]);
  and and_1 (and_1_out, not_1_out, not_2_out, not_3_out, in_1[1]);
  and and_2 (and_2_out, in_1[5], in_1[4], in_1[3], not_4_out, not_5_out, not_6_out);
  and and_3 (and_3_out, in_1[5], in_1[4], in_1[3], in_1[2], in_1[1], in_1[0]);
  and and_4 (and_4_out, not_7_out, in_1[3], in_1[1]);
  and and_5 (and_5_out, not_8_out, in_1[3], in_1[2]);
  and and_6 (and_6_out, not_9_out, in_1[0]);
  and and_7 (and_7_out, not_10_out, in_1[1], not_11_out);
  and and_8 (and_8_out, not_12_out, in_1[2]);
  and and_9 (and_9_out, in_1[2], in_1[1], not_13_out);
  and and_10 (and_10_out, not_14_out, in_1[3], not_15_out, not_16_out);
  and and_11 (and_11_out, not_17_out, not_18_out, not_19_out, not_20_out);
  and and_12 (and_12_out, in_1[3], in_1[2], not_21_out);
  and and_13 (and_13_out, in_1[5], in_1[2]);
  or or_1 (out_2[3], and_1_out, and_2_out, and_3_out);
  or or_2 (out_2[2], and_4_out, and_5_out);
  or or_3 (out_2[1], and_6_out, and_7_out, and_8_out, and_9_out, and_10_out);
  or or_4 (out_2[0], and_11_out, and_12_out, and_13_out);
  // Probe on out_2
endmodule

module OpFuncDec (
  input  [3:0] OpCode,
  input  [5:0] FunCode,
  output [3:0] out_3,
  output out_4
);

  wire and_2_out, and_3_out, and_4_out, and_5_out, and_6_out, and_7_out, and_8_out, and_9_out, and_10_out,
       IS0, not_1_out, not_2_out, not_3_out, not_4_out, not_5_out, not_6_out, not_7_out, not_8_out,
       not_9_out, not_10_out, not_11_out, not_12_out, not_13_out, not_14_out, not_15_out, not_16_out,
       or_1_out;

  and and_1 (IS0, ~OpCode[3], ~OpCode[2], ~OpCode[1], OpCode[0]);  // AND_Gate
  and and_2 (and_2_out, ~FunCode[5], FunCode[4], ~FunCode[3], ~FunCode[2], ~FunCode[1], ~FunCode[0]);  // AND_Gate
  and and_3 (and_3_out, ~FunCode[5], FunCode[4], ~FunCode[3], ~FunCode[2], FunCode[1], ~FunCode[0]);  // AND_Gate
  or or_1 (or_1_out, and_2_out, and_3_out);
  not not_1 (not_1_out, OpCode[2]);
  not not_2 (not_2_out, OpCode[1]);
  not not_3 (not_3_out, FunCode[5]);
  not not_4 (not_4_out, FunCode[4]);
  not not_5 (not_5_out, FunCode[2]);
  not not_6 (not_6_out, FunCode[1]);
  not not_7 (not_7_out, FunCode[0]);
  and and_4 (and_4_out, OpCode[3], OpCode[0]);
  not not_8 (not_8_out, OpCode[2]);
  not not_9 (not_9_out, FunCode[5]);
  not not_10 (not_10_out, FunCode[4]);
  not not_11 (not_11_out, FunCode[2]);
  not not_12 (not_12_out, FunCode[1]);
  not not_13 (not_13_out, FunCode[0]);
  not not_14 (not_14_out, OpCode[3]);
  not not_15 (not_15_out, OpCode[1]);
  not not_16 (not_16_out, FunCode[0]);
  and and_5 (and_5_out, not_1_out, not_2_out, OpCode[0], not_3_out, not_4_out, FunCode[3], not_5_out, not_6_out, not_7_out);
  or or_2 (out_3[2], OpCode[2], and_4_out);
  and and_6 (and_6_out, not_8_out, OpCode[0], not_9_out, not_10_out, FunCode[3], not_11_out, not_12_out, not_13_out);
  and and_7 (and_7_out, OpCode[3], FunCode[3]);
  and and_8 (and_8_out, not_14_out, OpCode[0]);
  and and_9 (and_9_out, OpCode[0], FunCode[3]);
  and and_10 (and_10_out, OpCode[3], not_15_out, not_16_out);
  and and_11 (out_4, IS0, or_1_out);
  or or_3 (out_3[3], and_5_out, OpCode[3]);
  or or_4 (out_3[1], and_6_out, OpCode[1], and_7_out);
  or or_5 (out_3[0], and_8_out, and_9_out, and_10_out);
  // Probe on out_3
endmodule
