// Logisim project ALU.circ as structural Verilog: 8 circuits, main circuit ALU
module ALU (
  input  [31:0] in_1,
  input  [31:0] in_2,
  input  [3:0] in_3,
  output Sign,
  output Equal,
  output [31:0] Result,
  output [31:0] Helper_Result,
  output Zero_Flag
);

  wire CF, comparator_1_lt, comparator_2_lt, OF, rnd_Clock;
  wire [1:0] n32_bit_adder_with_overflow_detection_1_out_5,
       n32_bit_substractor_with_overflow_detection_1_out_5;
  wire [31:0] and_1_out, bit_extender_1_out, bit_extender_2_out, divider_1_out, divider_1_rem,
       multiplier_1_cout, multiplier_1_out, n32_bit_adder_with_overflow_detection_1_out_6,
       n32_bit_substractor_with_overflow_detection_1_out_6, nor_1_out, or_1_out, random_1_out, shifter_1_out,
       shifter_2_out, shifter_3_out, signeddiv_1_multhigh, signeddiv_1_multlow, unsignedmult_1_hi,
       unsignedmult_1_lo, xor_1_out;

  // Probe on in_1
  // Probe on in_1
  // Probe on in_2
  // Probe on in_2
  // Probe on in_1
  Clock clock_1 (.out(rnd_Clock));
  // Probe on in_3
  _32_bit_Adder_With_Overflow_Detection u_32_bit_adder_with_overflow_detection_1 (
    .out_4(n32_bit_adder_with_overflow_detection_1_out_5[1]), .in_1(in_1), .in_2(in_2),
    .out_6(n32_bit_adder_with_overflow_detection_1_out_6),
    .out_5(n32_bit_adder_with_overflow_detection_1_out_5[0]));  // open: in_3
  _32_bit_Substractor_With_Overflow_Detection u_32_bit_substractor_with_overflow_detection_1 (
    .out_4(n32_bit_substractor_with_overflow_detection_1_out_5[1]),
    .out_5(n32_bit_substractor_with_overflow_detection_1_out_5[0]), .in_1(in_1), .in_2(in_2),
    .out_6(n32_bit_substractor_with_overflow_detection_1_out_6));  // open: in_3
  Shifter #(.width(32)) shifter_1 (.in(in_1), .\dist (in_2[4:0]), .out(shifter_1_out));
  Shifter #(.width(32), .shift("lr")) shifter_2 (.in(in_1), .\dist (in_2[4:0]), .out(shifter_2_out));
  assign and_1_out = in_1 & in_2;  // AND_Gate and_1, 32 bits wide
  Shifter #(.width(32), .shift("ar")) shifter_3 (.in(in_1), .\dist (in_2[4:0]), .out(shifter_3_out));
  assign or_1_out = in_1 | in_2;  // OR_Gate or_1, 32 bits wide
  assign nor_1_out = ~(in_1 | in_2);  // NOR_Gate nor_1, 32 bits wide
  assign xor_1_out = in_1 ^ in_2;  // XOR_Gate xor_1, 32 bits wide
  Comparator #(.width(32)) comparator_1 (.a(in_1), .b(in_2), .lt(comparator_1_lt));  // open: gt, eq
  Random #(.width(32)) random_1 (.clk(rnd_Clock), .next(1'b1), .out(random_1_out));  // open: clr
  Comparator #(.width(32), .mode("unsigned")) comparator_2 (
    .a(in_1), .b(in_2), .eq(Equal), .lt(comparator_2_lt));  // open: gt
  Multiplier #(.width(32)) multiplier_1 (
    .a(in_1), .b(in_2), .out(multiplier_1_out), .cout(multiplier_1_cout));  // open: cin
  SignedDiv signeddiv_1 (.in_1(in_1), .in_2(in_2), .MultLow(signeddiv_1_multlow), .MultHigh(signeddiv_1_multhigh));
  UnsignedMult unsignedmult_1 (.A(in_1), .B(in_2), .Hi(unsignedmult_1_hi), .Lo(unsignedmult_1_lo));
  Divider #(.width(32)) divider_1 (.a(in_1), .b(in_2), .out(divider_1_out), .rem(divider_1_rem));  // open: upper
  // Probe on Result
  // Probe on Result
  Multiplexer #(.select(4), .width(2)) multiplexer_1 (
    .in0(n32_bit_adder_with_overflow_detection_1_out_5),
    .in1(n32_bit_substractor_with_overflow_detection_1_out_5), .in2(2'b00), .in3(2'b00), .in4(2'b00),
    .in5(2'b00), .in6(2'b00), .in7(2'b00), .in8(2'b00), .in9(2'b00), .in10(2'b00), .in11(2'b00),
    .in12(2'b00), .in13(2'b00), .in14(2'b00), .in15(2'b00), .out({OF, CF}), .sel(in_3));  // open: en
  // Probe on Helper_Result
  assign bit_extender_1_out = {{31{1'b0}}, comparator_1_lt};  // Bit_Extender bit_extender_1
  assign bit_extender_2_out = {{31{1'b0}}, comparator_2_lt};  // Bit_Extender bit_extender_2
  Multiplexer #(.select(4), .width(32)) multiplexer_2 (
    .in0({32{1'b0}}), .in1({32{1'b0}}), .in2({32{1'b0}}), .in3({32{1'b0}}), .in4({32{1'b0}}),
    .in5({32{1'b0}}), .in6({32{1'b0}}), .in7({32{1'b0}}), .in8({32{1'b0}}), .in9({32{1'b0}}),
    .in10({32{1'b0}}), .in11({32{1'b0}}), .in12(multiplier_1_cout), .in13(signeddiv_1_multhigh),
    .in14(unsignedmult_1_hi), .in15(divider_1_rem), .out(Helper_Result), .sel(in_3));  // open: en
  Multiplexer #(.select(4), .width(32)) multiplexer_3 (
    .in0(n32_bit_adder_with_overflow_detection_1_out_6),
    .in1(n32_bit_substractor_with_overflow_detection_1_out_6), .in2(shifter_1_out), .in3(shifter_2_out),
    .in4(and_1_out), .in5(shifter_3_out), .in6(or_1_out), .in7(nor_1_out), .in8(xor_1_out),
    .in9(bit_extender_1_out), .in10(random_1_out), .in11(bit_extender_2_out), .in12(multiplier_1_out),
    .in13(signeddiv_1_multlow), .in14(unsignedmult_1_lo), .in15(divider_1_out), .out(Result), .sel(in_3));  // open: en
  Comparator #(.width(32)) comparator_3 (.a({32{1'b0}}), .b(Result), .eq(Zero_Flag));  // open: gt, lt

  assign Sign = Result[31];

  // Other names for the same wires on the sheet: A[31:0] = in_1; B[31:0] = in_2; Help_Result[31:0] = Helper_Result;
  //   Main_Result[31:0] = Result; OP[3:0] = in_3; Zero = Zero_Flag

  // Notes on the sheet:
  //   INPUTS
  //   Added With OF
  //   Substractor With OF
  //   AND
  //   OR
  //   NOR
  //   XOR
  //   Set Less Than
  //   Set Random
  //   Set Less Than(U)
  //   Signed Mult
  //   Signed Div
  //   Unsigned Mult
  //   Unsigned Div
  //   Logical Left
  //   Logical Right
  //   Arithmetic Right
  //   OUTPUTS
endmodule

module SignedMult (
  input  [31:0] in_1,
  input  [31:0] in_2,
  output [31:0] MultLow,
  output [31:0] MultHigh
);

  wire neg_1_out_3, SignResult;
  wire [31:0] absA, absB, multiplier_1_cout, multiplier_1_out, neg_1_out_2, neg_2_out_2;

  xor xor_1 (SignResult, in_1[31], in_2[31]);
  // Abs abs_1: pin names not known; wires that end beside it: in_1, in_1[31], absA
  // Abs abs_2: pin names not known; wires that end beside it: in_2, in_2[31], absB
  Multiplier #(.width(32)) multiplier_1 (
    .a(absA), .b(absB), .out(multiplier_1_out), .cout(multiplier_1_cout));  // open: cin
  Neg neg_1 (.Data_A(multiplier_1_out), .out_2(neg_1_out_2), .out_3(neg_1_out_3));
  Neg neg_2 (.Data_A(multiplier_1_cout), .out_2(neg_2_out_2));  // open: out_3
  Multiplexer #(.width(32)) multiplexer_1 (
    .in0(multiplier_1_out), .in1(neg_1_out_2), .out(MultLow), .sel(SignResult));  // open: en
  Multiplexer #(.width(32)) multiplexer_2 (
    .in0(multiplier_1_cout), .in1(neg_2_out_2), .out(MultHigh), .sel(SignResult));  // open: en
  // Probe on MultLow
  // Probe on MultHigh

  // Other names for the same wires on the sheet: A[31:0] = in_1; SignA = in_1[31]; B[31:0] = in_2; SignB = in_2[31]
endmodule

module Abs (
  input  [31:0] Data_A,
  output [31:0] Abs_A
);

  wire [31:0] adder_1_out, not_1_out;

  assign not_1_out = ~Data_A;  // NOT_Gate not_1, 32 bits wide
  Adder #(.width(32)) adder_1 (.a(not_1_out), .b(32'h1), .out(adder_1_out));  // open: cin, cout
  Multiplexer #(.width(32)) multiplexer_1 (.in0(Data_A), .in1(adder_1_out), .out(Abs_A), .sel(Data_A[31]));  // open: en
endmodule

module Neg (
  input  [31:0] Data_A,
  output [31:0] out_2,
  output out_3
);

  wire [31:0] not_1_out;

  assign not_1_out = ~Data_A;  // NOT_Gate not_1, 32 bits wide
  Adder #(.width(32)) adder_1 (.a(not_1_out), .b(32'h1), .out(out_2), .cout(out_3));  // open: cin

  // Other names for the same wires on the sheet: A[31:0] = Data_A
endmodule

module SignedDiv (
  input  [31:0] in_1,
  input  [31:0] in_2,
  output [31:0] MultLow,
  output [31:0] MultHigh
);

  wire SignResult;
  wire [31:0] absA, absB, divider_1_out, divider_1_rem, neg_1_out_2, neg_2_out_2;

  xor xor_1 (SignResult, in_1[31], in_2[31]);
  // Abs abs_1: pin names not known; wires that end beside it: in_1, in_1[31], absA
  // Abs abs_2: pin names not known; wires that end beside it: in_2, in_2[31], absB
  Divider #(.width(32)) divider_1 (.a(absA), .b(absB), .out(divider_1_out), .rem(divider_1_rem));  // open: upper
  Neg neg_1 (.Data_A(divider_1_out), .out_2(neg_1_out_2));  // open: out_3
  Neg neg_2 (.Data_A(divider_1_rem), .out_2(neg_2_out_2));  // open: out_3
  Multiplexer #(.width(32)) multiplexer_1 (
    .in0(divider_1_out), .in1(neg_1_out_2), .out(MultLow), .sel(SignResult));  // open: en
  Multiplexer #(.width(32)) multiplexer_2 (
    .in0(divider_1_rem), .in1(neg_2_out_2), .out(MultHigh), .sel(SignResult));  // open: en
  // Probe on MultLow
  // Probe on MultHigh

  // Other names for the same wires on the sheet: A[31:0] = in_1; SignA = in_1[31]; B[31:0] = in_2; SignB = in_2[31]
endmodule

module _32_bit_Adder_With_Overflow_Detection (
  input  [31:0] in_1,
  input  [31:0] in_2,
  input  in_3,
  output out_4,
  output out_5,
  output [31:0] out_6
);

  wire adder_1_cout;

  // Probe on in_1
  Adder #(.width(31)) adder_1 (.a(in_1[30:0]), .b(in_2[30:0]), .out(out_6[30:0]), .cin(in_3), .cout(adder_1_cout));
  Adder #(.width(1)) adder_2 (.a(in_1[31]), .b(in_2[31]), .out(out_6[31]), .cin(adder_1_cout), .cout(out_4));
  // Probe on in_2
  xor xor_1 (out_5, adder_1_cout, out_4);
  // Probe on out_6

  // Other names for the same wires on the sheet: A[31:0] = in_1; B[31:0] = in_2; c_in = in_3; CF = out_4; OF = out_5;
  //   Result[31:0] = out_6
endmodule

module _32_bit_Substractor_With_Overflow_Detection (
  input  [31:0] in_1,
  input  [31:0] in_2,
  input  in_3,
  output out_4,
  output out_5,
  output [31:0] out_6
);

  wire subtractor_1_bout;

  // Probe on in_1
  Subtractor #(.width(31)) subtractor_1 (
    .a(in_1[30:0]), .b(in_2[30:0]), .out(out_6[30:0]), .bin(in_3), .bout(subtractor_1_bout));
  Subtractor #(.width(1)) subtractor_2 (
    .a(in_1[31]), .b(in_2[31]), .out(out_6[31]), .bin(subtractor_1_bout), .bout(out_4));
  // Probe on in_2
  xor xor_1 (out_5, subtractor_1_bout, out_4);
  // Probe on out_6

  // Other names for the same wires on the sheet: A[31:0] = in_1; B[31:0] = in_2; b_in = in_3; CF = out_4; OF = out_5;
  //   Result[31:0] = out_6
endmodule

module UnsignedMult (
  input  [31:0] A,
  input  [31:0] B,
  output [31:0] Hi,
  output [31:0] Lo
);

  wire adder_1_cout, adder_5_cout, and_1_out;
  wire [31:0] A_t, and_2_out, and_3_out, B_t, bit_extender_3_out, bit_extender_4_out, bit_extender_5_out,
       bit_extender_6_out, bit_extender_8_out, Hi1, Hi2, Hi3, Hi4, Hi5, Hi6, Hi7, Hi8, Hi9, Hi10, Lo1, Lo3,
       Lo4, Lo5;

  assign A_t = {{1{1'b0}}, A[30:0]};  // Bit_Extender bit_extender_1
  assign B_t = {{1{1'b0}}, B[30:0]};  // Bit_Extender bit_extender_2
  and and_1 (and_1_out, A[31], B[31]);
  Multiplier #(.width(32)) multiplier_1 (.a(A_t), .b(B_t), .out(Lo1), .cout(Hi1));  // open: cin
  assign bit_extender_3_out = {{31{1'b0}}, and_1_out};  // Bit_Extender bit_extender_3
  assign bit_extender_4_out = {{31{A[31]}}, A[31]};  // Bit_Extender bit_extender_4
  assign bit_extender_5_out = {{31{B[31]}}, B[31]};  // Bit_Extender bit_extender_5
  Shifter #(.width(32)) shifter_1 (.in(bit_extender_3_out), .\dist (5'b11110), .out(Hi2));
  assign and_2_out = bit_extender_4_out & B_t;  // AND_Gate and_2, 32 bits wide
  assign and_3_out = bit_extender_5_out & A_t;  // AND_Gate and_3, 32 bits wide
  assign bit_extender_6_out = {{31{1'b0}}, and_2_out[0]};  // Bit_Extender bit_extender_6
  assign Hi3 = {{1{1'b0}}, and_2_out[31:1]};  // Bit_Extender bit_extender_7
  assign bit_extender_8_out = {{31{1'b0}}, and_3_out[0]};  // Bit_Extender bit_extender_8
  assign Hi4 = {{1{1'b0}}, and_3_out[31:1]};  // Bit_Extender bit_extender_9
  Shifter #(.width(32)) shifter_2 (.in(bit_extender_6_out), .\dist ({5{1'b1}}), .out(Lo3));
  Shifter #(.width(32)) shifter_3 (.in(bit_extender_8_out), .\dist ({5{1'b1}}), .out(Lo4));
  Adder #(.width(32)) adder_1 (.a(Lo3), .b(Lo4), .out(Lo5), .cout(adder_1_cout));  // open: cin
  Adder #(.width(32)) adder_2 (.a(Hi3), .b(Hi4), .out(Hi6));  // open: cin, cout
  Adder #(.width(32)) adder_3 (.a(Hi2), .b(Hi6), .out(Hi7));  // open: cin, cout
  Adder #(.width(32)) adder_4 (.a(Hi1), .b(Hi7), .out(Hi8));  // open: cin, cout
  Adder #(.width(32)) adder_5 (.a(Lo1), .b(Lo5), .out(Lo), .cout(adder_5_cout));  // open: cin
  Adder #(.width(32)) adder_6 (.a(Hi8), .b(Hi9), .out(Hi10));  // open: cin, cout
  Adder #(.width(32)) adder_7 (.a(Hi10), .b(Hi5), .out(Hi));  // open: cin, cout
  assign Hi5 = {{31{1'b0}}, adder_1_cout};  // Bit_Extender bit_extender_10
  assign Hi9 = {{31{1'b0}}, adder_5_cout};  // Bit_Extender bit_extender_11

  // Other names for the same wires on the sheet: As = A[31]; Bs = B[31]
endmodule
