// Logisim project Branch Control.circ as structural Verilog: 1 circuit, main circuit main
module main (
  input  [15:0] in_1,
  input  [31:0] PC_out
);

  wire [31:0] Branch_target_address, PC_plus_4, shifter_1_out, undriven;

  Bit_Extender #(.in_width(16), .out_width(32), .\type ("sign")) bit_extender_1 ();  // open: in, out
  Adder #(.width(32)) adder_1 (.a(PC_out), .b(32'h4), .out(PC_plus_4));  // open: cin, cout
  Shifter #(.width(32)) shifter_1 (.in(undriven), .\dist (5'b00010), .out(shifter_1_out));
  Adder #(.width(32)) adder_2 (.a(PC_plus_4), .b(shifter_1_out), .out(Branch_target_address));  // open: cin, cout

  // Other names for the same wires on the sheet: Offset[15:0] = in_1

  // Notes on the sheet:
  //   BRANCH CONTROL
endmodule
