// Logisim project DataPath.circ as structural Verilog: 2 circuits, main circuit main
module main (
  input  in_1,
  input  in_2,
  input  in_3,
  input  [1:0] in_4,
  input  [1:0] in_5,
  input  in_6,
  input  in_7,
  input  in_8,
  input  in_9,
  input  [1:0] in_10,
  input  [3:0] in_11,
  input  [1:0] in_12,
  input  in_13,
  input  [6:0] KBDInput,
  input  in_15,
  input  in_16,
  input  in_17,
  input  in_18,
  input  in_19,
  input  in_20,
  input  in_21,
  input  in_22,
  input  [31:0] RAM_0,
  input  [31:0] RAM_1,
  input  [31:0] RAM_2,
  input  [31:0] RAM_3,
  input  [3:0] WT,
  input  [3:0] RT,
  output [6:0] TTY_Output,
  output [5:0] OpCode,
  output [5:0] FuncCode,
  output out_32,
  output out_33,
  output out_34,
  output [3:0] MASK,
  output [31:0] RAM_0_2,
  output [31:0] RAM_1_2,
  output [31:0] RAM_2_2,
  output [31:0] RAM_3_2,
  output [15:0] RAM_Adress,
  output out_41,
  output out_42
);

  wire and_1_out, branchunit_1_do_branch, or_1_out;
  wire [4:0] multiplexer_3_out, multiplexer_4_out, multiplexer_5_out;
  wire [15:6] Instr_q;
  wire [25:16] Instr_q_2;
  wire [27:0] shifter_2_out;
  wire [31:0] A_q, ALUOut_q, B_q, bit_extender_1_out, bit_extender_2_out, bit_extender_3_out,
       cache_unit_1_readdata, Data_q, Hi_in, Hi_out, HiLo_in, KbdIn, Lo_in, Lo_out, main_2_b,
       multiplexer_6_out, multiplexer_8_out, multiplexer_9_out, multiplexer_10_out, multiplexer_11_out, PC,
       RAM_Control, shifter_1_out;
  wire [31:7] main_2_a;

  PC_main main_1 (.Input(multiplexer_11_out), .Enable(or_1_out), .Clk(in_1), .Output(PC), .Reset(in_22));
  Multiplexer #(.width(32)) multiplexer_1 (
    .in0(PC), .in1(ALUOut_q), .out({RAM_Control[31:20], RAM_Adress, RAM_Control[3:0]}), .sel(in_3));  // open: en
  Cache_Unit cache_unit_1 (
    .Adress({RAM_Control[31:20], RAM_Adress, RAM_Control[3:0]}), .WriteData(B_q), .MemRead(in_21),
    .MemWrite(in_8), .Clk(in_1), .Reset(in_22), .RAM_O0(RAM_0), .RAM_O1(RAM_1), .RAM_O2(RAM_2),
    .RAM_O3(RAM_3), .RT(WT), .WT(RT), .ReadData(cache_unit_1_readdata), .Stall(out_34), .To_CS(out_41),
    .To_RW(out_42), .To_I0(RAM_0_2), .To_I1(RAM_1_2), .To_I2(RAM_2_2), .To_I3(RAM_3_2));
  assign bit_extender_1_out = {{25{KBDInput[6]}}, KBDInput};  // Bit_Extender bit_extender_1
  // Probe on cache_unit_1_readdata
  Register #(.width(32)) Instr (
    .D(cache_unit_1_readdata), .en(in_6), .Q({OpCode, Instr_q_2, Instr_q, FuncCode}), .clk(in_1), .clr(in_22));
  Register #(.width(32)) Data (.D(cache_unit_1_readdata), .Q(Data_q), .clk(in_1), .clr(in_22));  // open: en
  Multiplexer #(.width(32), .enable("false")) multiplexer_2 (
    .in0({32{1'b1}}), .in1(bit_extender_1_out), .out(KbdIn), .sel(in_16));
  Multiplexer #(.width(5), .enable("false")) multiplexer_3 (
    .in0(Instr_q_2[25:21]), .in1({5{1'b1}}), .out(multiplexer_3_out), .sel(in_17));
  Multiplexer #(.width(5), .enable("false")) multiplexer_4 (
    .in0(Instr_q_2[20:16]), .in1(Instr_q_2[25:21]), .out(multiplexer_4_out), .sel(in_18));
  Multiplexer #(.select(2), .width(5)) multiplexer_5 (
    .in0(Instr_q_2[20:16]), .in1(Instr_q[15:11]), .in2({5{1'b1}}), .out(multiplexer_5_out), .sel(in_10));  // open: in3, en
  Multiplexer #(.select(2), .width(32)) multiplexer_6 (
    .in0(Data_q), .in1(ALUOut_q), .in2(KbdIn), .in3(HiLo_in), .out(multiplexer_6_out), .sel(in_12));  // open: en
  Demultiplexer #(.select(2), .enable("false")) demultiplexer_1 (
    .out0(MASK[0]), .out1(MASK[1]), .out2(MASK[2]), .out3(MASK[3]), .in(1'b1), .sel(RAM_Control[3:2]));
  // Probe on {main_2_a, TTY_Output}
  Register_File_main main_2 (
    .Data_Input(multiplexer_6_out), .reset(in_22), .R_W(in_13), .clock(in_1), .SOp(in_17),
    .Data_Address(multiplexer_5_out), .Selector_A(multiplexer_3_out), .Selector_B(multiplexer_4_out),
    .High_in(Hi_in), .Low_in(Lo_in), .Hi_Lo_enable(in_20), .A({main_2_a, TTY_Output}), .B(main_2_b),
    .High_Out(Hi_out), .Low_Out(Lo_out));  // open: PC_enable, Stack_Pointer
  assign bit_extender_2_out = {{16{1'b0}}, {Instr_q, FuncCode}};  // Bit_Extender bit_extender_2
  assign bit_extender_3_out = {{16{Instr_q[15]}}, {Instr_q, FuncCode}};  // Bit_Extender bit_extender_3
  Multiplexer #(.width(32), .enable("false")) multiplexer_7 (.in0(Hi_out), .in1(Lo_out), .out(HiLo_in), .sel(in_19));
  Register #(.width(32)) A (.D({main_2_a, TTY_Output}), .Q(A_q), .clk(in_1), .clr(in_22));  // open: en
  Register #(.width(32)) B (.D(main_2_b), .Q(B_q), .clk(in_1), .clr(in_22));  // open: en
  Multiplexer #(.width(32)) multiplexer_8 (
    .in0(bit_extender_3_out), .in1(bit_extender_2_out), .out(multiplexer_8_out), .sel(in_15));  // open: en
  // Probe on A_q
  Shifter #(.width(32)) shifter_1 (.in(bit_extender_3_out), .\dist (5'b00010), .out(shifter_1_out));
  Shifter #(.width(28)) shifter_2 (
    .in({OpCode[1:0], Instr_q_2, Instr_q, FuncCode}), .\dist (5'b00010), .out(shifter_2_out));
  Multiplexer #(.width(32)) multiplexer_9 (.in0(PC), .in1(A_q), .out(multiplexer_9_out), .sel(in_2));  // open: en
  Multiplexer #(.select(2), .width(32), .enable("false")) multiplexer_10 (
    .in0(B_q), .in1(32'h4), .in2(multiplexer_8_out), .in3(shifter_1_out), .out(multiplexer_10_out), .sel(in_4));
  BranchUnit branchunit_1 (.OpCode(OpCode), .Do_Branch(branchunit_1_do_branch), .Sign(out_33), .Zero(out_32));
  ALU alu_1 (
    .in_1(multiplexer_9_out), .in_2(multiplexer_10_out), .in_3(in_11), .Result(Lo_in), .Helper_Result(Hi_in),
    .Zero_Flag(out_32), .Sign(out_33));  // open: Equal
  and and_1 (and_1_out, branchunit_1_do_branch, in_7);
  Register #(.width(32)) ALUOut (.D(Lo_in), .Q(ALUOut_q), .clk(in_1), .clr(in_22));  // open: en
  or or_1 (or_1_out, in_9, and_1_out);
  Multiplexer #(.select(2), .width(32), .enable("false")) multiplexer_11 (
    .in0(Lo_in), .in1(ALUOut_q), .in2({PC[31:28], shifter_2_out}), .out(multiplexer_11_out), .sel(in_5));  // open: in3

  // Other names for the same wires on the sheet: ALUControl[3:0] = in_11; ALUSrcA = in_2; ALUSrcB[1:0] = in_4;
  //   Branch = in_7; Clk = in_1; HiLo_selector = in_19; HiLoEn = in_20; IorD = in_3; IRWrite = in_6; MemRead = in_21;
  //   MemtoReg[1:0] = in_12; MemWrite = in_8; PCSrc[1:0] = in_5; PCWrite = in_9; R_W = in_13; RAM_0_in[31:0] = RAM_0;
  //   RAM_0_out[31:0] = RAM_0_2; RAM_1_in[31:0] = RAM_1; RAM_1_out[31:0] = RAM_1_2; RAM_2_in[31:0] = RAM_2;
  //   RAM_2_out[31:0] = RAM_2_2; RAM_3_in[31:0] = RAM_3; RAM_3_out[31:0] = RAM_3_2; RAM_Control[19:4] = RAM_Adress;
  //   RegDst[1:0] = in_10; _0 = in_22; Reset = in_22; Sign = out_33; StackOp = in_17; StopFSM = out_34;
  //   To_Cs = out_41; To_Rw = out_42; UseRsAsB = in_18; Z_S = in_15; Zero = out_32

  // Notes on the sheet:
  //   ALU+4
endmodule

module BranchUnit (
  input  Sign,
  input  Zero,
  input  [5:0] OpCode,
  output Do_Branch
);

  wire and_1_out, and_2_out, and_3_out, and_4_out, and_5_out, comparator_1_eq, comparator_2_eq,
       comparator_3_eq, comparator_4_eq, comparator_5_eq, nor_1_out, or_1_out;

  Comparator #(.width(6)) comparator_1 (.a(OpCode), .b(6'b000100), .eq(comparator_1_eq));  // open: gt, lt
  Comparator #(.width(6)) comparator_2 (.a(OpCode), .b(6'b000101), .eq(comparator_2_eq));  // open: gt, lt
  Comparator #(.width(6)) comparator_3 (.a(OpCode), .b(6'b000001), .eq(comparator_3_eq));  // open: gt, lt
  Comparator #(.width(6)) comparator_4 (.a(OpCode), .b(6'b000111), .eq(comparator_4_eq));  // open: gt, lt
  Comparator #(.width(6)) comparator_5 (.a(OpCode), .b(6'b000110), .eq(comparator_5_eq));  // open: gt, lt
  and and_1 (and_1_out, comparator_1_eq, Zero);
  and and_2 (and_2_out, comparator_2_eq, ~Zero);  // AND_Gate
  and and_3 (and_3_out, comparator_3_eq, Sign);
  and and_4 (and_4_out, comparator_4_eq, nor_1_out);
  nor nor_1 (nor_1_out, Zero, Sign);
  and and_5 (and_5_out, comparator_5_eq, or_1_out);
  or or_1 (or_1_out, Zero, Sign);
  or or_2 (Do_Branch, and_1_out, and_2_out, and_3_out, and_4_out, and_5_out);

  // Notes on the sheet:
  //   BEQ
  //   BNE
  //   BLTZ
  //   BGTZ
  //   BLEZ
endmodule
