// Logisim project PC.circ as structural Verilog: 1 circuit, main circuit main
module main (
  input  [31:0] Input,
  input  Enable,
  input  Clk,
  input  Reset,
  output [31:0] Output
);

  Register #(.width(32)) register_1 (.D(Input), .en(Enable), .Q(Output), .clk(Clk), .clr(Reset));

  // Notes on the sheet:
  //   PROGRAM COUNTER
endmodule
