// Logisim project inst_dataMemory.circ as structural Verilog: 2 circuits, main circuit main
module main (
  input  WE,
  input  Clock,
  input  [31:0] Instruction,
  input  [31:0] Write_Data,
  output [31:0] RD
);

  wire and_1_out, and_2_out, and_3_out, and_4_out, and_5_out, and_6_out, and_7_out, and_8_out,
       decoder_1_out0, decoder_1_out1, decoder_1_out2, decoder_1_out3, decoder_1_out4, decoder_1_out5,
       decoder_1_out6, decoder_1_out7;
  wire [31:0] block_1_o1, block_2_o1, block_3_o1, block_4_o1, block_5_o1, block_6_o1, block_7_o1, block_8_o1;

  // Probe on Instruction[6:4]
  Decoder #(.select(3)) decoder_1 (
    .out0(decoder_1_out0), .out1(decoder_1_out1), .out2(decoder_1_out2), .out3(decoder_1_out3),
    .out4(decoder_1_out4), .out5(decoder_1_out5), .out6(decoder_1_out6), .out7(decoder_1_out7),
    .sel(Instruction[6:4]));  // open: en
  and and_1 (and_1_out, decoder_1_out0, WE);
  and and_2 (and_2_out, decoder_1_out1, WE);
  and and_3 (and_3_out, decoder_1_out2, WE);
  and and_4 (and_4_out, decoder_1_out3, WE);
  and and_5 (and_5_out, decoder_1_out4, WE);
  and and_6 (and_6_out, decoder_1_out5, WE);
  and and_7 (and_7_out, decoder_1_out6, WE);
  and and_8 (and_8_out, decoder_1_out7, WE);
  Block block_1 (.in_1(Clock), .in_2(and_1_out), .in_3(Instruction[3:2]), .O1(block_1_o1), .WD(Write_Data));
  Block block_2 (.in_1(Clock), .in_2(and_2_out), .in_3(Instruction[3:2]), .O1(block_2_o1), .WD(Write_Data));
  Block block_3 (.in_2(and_3_out), .in_3(Instruction[3:2]), .O1(block_3_o1), .WD(Write_Data));  // open: in_1
  Block block_4 (.in_1(Clock), .in_2(and_4_out), .in_3(Instruction[3:2]), .O1(block_4_o1), .WD(Write_Data));
  Block block_5 (.in_1(Clock), .in_2(and_5_out), .in_3(Instruction[3:2]), .O1(block_5_o1), .WD(Write_Data));
  Block block_6 (.in_1(Clock), .in_2(and_6_out), .in_3(Instruction[3:2]), .O1(block_6_o1), .WD(Write_Data));
  Block block_7 (.in_1(Clock), .in_2(and_7_out), .in_3(Instruction[3:2]), .O1(block_7_o1), .WD(Write_Data));
  Block block_8 (.in_1(Clock), .in_2(and_8_out), .in_3(Instruction[3:2]), .O1(block_8_o1), .WD(Write_Data));
  Multiplexer #(.select(3), .width(32), .enable("false")) multiplexer_1 (
    .in0(block_1_o1), .in1(block_2_o1), .in2(block_3_o1), .in3(block_4_o1), .in4(block_5_o1),
    .in5(block_6_o1), .in6(block_7_o1), .in7(block_8_o1), .out(RD), .sel(Instruction[6:4]));

  // Other names for the same wires on the sheet: A[31:0] = Instruction; wordindex[1:0] = Instruction[3:2];
  //   blockindex[2:0] = Instruction[6:4]; WD[31:0] = Write_Data
endmodule

module Block (
  input  in_1,
  input  in_2,
  input  [1:0] in_3,
  input  [31:0] WD,
  output [31:0] O1
);

  wire decoder_1_out0, decoder_1_out1, decoder_1_out2, decoder_1_out3, e1, e2, e3, e4;
  wire [31:0] W1_q, W2_q, W3_q, W4_q;

  Decoder #(.select(2)) decoder_1 (
    .out0(decoder_1_out0), .out1(decoder_1_out1), .out2(decoder_1_out2), .out3(decoder_1_out3), .sel(in_3));  // open: en
  and and_1 (e1, decoder_1_out0, in_2);
  and and_2 (e2, decoder_1_out1, in_2);
  and and_3 (e3, decoder_1_out2, in_2);
  and and_4 (e4, decoder_1_out3, in_2);
  Register #(.width(32)) W1 (.D(WD), .en(e1), .Q(W1_q), .clk(in_1));  // open: clr
  Register #(.width(32)) W2 (.D(WD), .en(e2), .Q(W2_q), .clk(in_1));  // open: clr
  Register #(.width(32)) W3 (.D(WD), .en(e3), .Q(W3_q), .clk(in_1));  // open: clr
  Register #(.width(32)) W4 (.en(e4), .Q(W4_q), .clk(in_1));  // open: D, clr
  Multiplexer #(.select(2), .width(32), .enable("false")) multiplexer_1 (
    .in0(W1_q), .in1(W2_q), .in2(W3_q), .in3(W4_q), .out(O1), .sel(in_3));

  // Other names for the same wires on the sheet: clock = in_1; we = in_2; wi[1:0] = in_3
endmodule
